// Logisim project CA_Assignment.circ as structural Verilog: 1 circuit, main circuit main
module main (
  input  [3:0] BR,
  input  [2:0] in_2,
  input  in_3
);

  wire and_1_out, and_2_out, and_3_out, and_4_out, and_5_out, and_6_out, and_7_out, and_8_out, and_9_out,
       and_10_out, and_11_out, clock_1_out, clock_2_out, comparator_1_eq, comparator_2_eq, comparator_2_gt,
       comparator_2_lt, d_ff_5_q, d_ff_6_q, d_ff_7_q, d_ff_8_q, d_ff_9_q, not_1_out, or_1_out, or_2_out,
       or_3_out, or_4_out, or_5_out, or_6_out, or_7_out, or_8_out;
  wire [2:0] counter_1_q;
  wire [3:0] adder_1_out, d_ff_4_q, subtractor_1_out;

  Clock clock_1 (.out(clock_1_out));
  or or_1 (or_1_out, or_5_out, and_3_out);
  or or_2 (or_2_out, or_8_out, and_3_out);
  D_Flip_Flop d_ff_1 (.clk(clock_1_out), .D(or_1_out), .Q(d_ff_4_q[3]), .en(not_1_out));  // open: Qn, preset, reset
  or or_3 (or_3_out, or_7_out, and_2_out);
  Adder #(.width(4)) adder_1 (.a(d_ff_4_q), .b(BR), .out(adder_1_out));  // open: cin, cout
  Counter #(.width(3), .max('h4), .ongoal("stay")) counter_1 (
    .load(in_3), .Q(counter_1_q), .clk(clock_2_out));  // open: D, count, carry, clr
  Clock clock_2 (.out(clock_2_out));
  D_Flip_Flop d_ff_2 (.clk(clock_1_out), .D(or_2_out), .Q(d_ff_4_q[2]), .en(not_1_out));  // open: Qn, preset, reset
  or or_4 (or_4_out, or_6_out, and_1_out);
  D_Flip_Flop d_ff_3 (.clk(clock_1_out), .D(or_3_out), .Q(d_ff_4_q[1]), .en(not_1_out));  // open: Qn, preset, reset
  not not_1 (not_1_out, comparator_1_eq);
  Comparator #(.width(3), .mode("unsigned")) comparator_1 (
    .a(in_2), .b(counter_1_q), .eq(comparator_1_eq));  // open: gt, lt
  D_Flip_Flop d_ff_4 (.clk(clock_1_out), .D(or_4_out), .Q(d_ff_4_q[0]), .en(not_1_out));  // open: Qn, preset, reset
  or or_5 (or_5_out, and_11_out, and_7_out);
  D_Flip_Flop d_ff_5 (.clk(clock_1_out), .D(d_ff_4_q[0]), .Q(d_ff_5_q), .en(not_1_out));  // open: Qn, preset, reset
  or or_6 (or_6_out, and_8_out, and_4_out);
  or or_7 (or_7_out, and_9_out, and_5_out);
  or or_8 (or_8_out, and_10_out, and_6_out);
  D_Flip_Flop d_ff_6 (.clk(clock_1_out), .D(d_ff_5_q), .Q(d_ff_6_q), .en(not_1_out));  // open: Qn, preset, reset
  and and_1 (and_1_out, d_ff_4_q[1], comparator_2_eq);
  and and_2 (and_2_out, d_ff_4_q[2], comparator_2_eq);
  and and_3 (and_3_out, d_ff_4_q[3], comparator_2_eq);
  and and_4 (and_4_out, adder_1_out[0], comparator_2_gt);
  and and_5 (and_5_out, adder_1_out[1], comparator_2_gt);
  and and_6 (and_6_out, adder_1_out[2], comparator_2_gt);
  and and_7 (and_7_out, adder_1_out[3], comparator_2_gt);
  D_Flip_Flop d_ff_7 (.clk(clock_1_out), .D(d_ff_8_q), .Q(d_ff_7_q), .en(not_1_out));  // open: Qn, preset, reset
  D_Flip_Flop d_ff_8 (.clk(clock_1_out), .D(d_ff_6_q), .Q(d_ff_8_q), .en(not_1_out));  // open: Qn, preset, reset
  Comparator #(.width(1), .mode("unsigned")) comparator_2 (
    .a(d_ff_9_q), .b(d_ff_7_q), .gt(comparator_2_gt), .eq(comparator_2_eq), .lt(comparator_2_lt));
  D_Flip_Flop d_ff_9 (.clk(clock_1_out), .D(d_ff_7_q), .Q(d_ff_9_q), .en(not_1_out));  // open: Qn, preset, reset
  and and_8 (and_8_out, subtractor_1_out[0], comparator_2_lt);
  and and_9 (and_9_out, subtractor_1_out[1], comparator_2_lt);
  and and_10 (and_10_out, subtractor_1_out[2], comparator_2_lt);
  and and_11 (and_11_out, subtractor_1_out[3], comparator_2_lt);
  Subtractor #(.width(4)) subtractor_1 (.a(BR), .b(d_ff_4_q), .out(subtractor_1_out));  // open: bin, bout

  // Notes on the sheet:
  //   Counter
  //   AC
  //   QR
  //   Q(n+1)
endmodule
